# Fritzing sketch Greenhouse_System_Schematic_And_Wiring (saved by Fritzing 1.0.5)
breadboards: 1

parts:
  Part1 = Arduino Mega 2560 (Rev3)
  Photoresistor = Photocell (LDR) [power=0.25W dark_resistance_@0.01lx=300kΩ light_resistance_@100lx=400Ω luminance=10lx package=THT]
  soil_moisture_sensor = Soil Moisture Sensor
  Ultrasonic_sensor = HC-SR04 Ultrasonic Distance Sensor
  Rain_drop_sensor = Rotary Potentiometer (Large) [maximum_resistance=100kΩ knob_status=50% power=0.5W package=THT]
  water_level_sensor = Rotary Potentiometer (Large) [maximum_resistance=100kΩ knob_status=50% power=0.5W package=THT]
  I2C_LCD = LCD1602-I2C
  relay_fan = KY-019 5V Relay Module [package="Breakout board"]
  relay_pump = KY-019 5V Relay Module [package="Breakout board"]
  SERVO1 = Tower Pro SG90 servo [part_number=101246]
  motor_fan = DC Motor [voltage_(max)=6V voltage_(min)=3V]
  passive_buzzer = Passive buzzer [package=THT]
  Red_led = smd LED [color="Red (633nm)" package="1206 [SMD]"]
  green_led = smd LED [color="Green (570nm)" package="1206 [SMD]"]
  Resistor_redled = Resistor [tolerance=±5% resistance=220 package="2010 [SMD]"]
  resistor_green_led = Resistor [tolerance=±5% resistance=220 package="2010 [SMD]"]
  resistor_photoresistor = Resistor [tolerance=±5% resistance=10k package="2010 [SMD]"]
  DHT11_1 = DHT11 module
  BAT1 = LIPO-2000mAh [package=lipo-2000]
  BAT2 = LIPO-2000mAh [package=lipo-2000]
  step_down(_motor_servo) = LM2596 step down module
  step_down_(pump) = LM2596 step down module
  Pump = DC Motor [voltage_(max)=6V voltage_(min)=3V]

nets:
  N1: Part1.A10, Rain_drop_sensor.wiper
  N2: Part1.A12, Photoresistor.pin_1, resistor_photoresistor.Pin_0
  N3: Part1.A15, SERVO1.Signal
  N4: Part1.A1, soil_moisture_sensor.SIG
  N5: Part1.D21/SCL, Part1.SCL, I2C_LCD.SCL
  N6: Part1.D20/SDA, Part1.SDA, I2C_LCD.SDA
  GND: Part1.GND, soil_moisture_sensor.GND, Ultrasonic_sensor.GND, Rain_drop_sensor.leg2, I2C_LCD.GND, relay_fan.-, relay_pump.-, SERVO1.GND, motor_fan.pin_2, passive_buzzer.pin2, Red_led.cathode, green_led.cathode, resistor_photoresistor.Pin_1, DHT11_1.GND, BAT1.-, step_down(_motor_servo).IN-, step_down(_motor_servo).OUT-, step_down_(pump).IN-, step_down_(pump).OUT-, Pump.pin_2
  N7: Part1.D13_PWM, DHT11_1.DATA
  N8: Part1.D12_PWM, passive_buzzer.pin1
  N9: Part1.D11_PWM, Resistor_redled.Pin_1
  N10: Part1.D10_PWM, resistor_green_led.Pin_1
  N11: Part1.D8_PWM, water_level_sensor.wiper
  VCC: Part1.5V, Photoresistor.pin_0, soil_moisture_sensor.VCC, Ultrasonic_sensor.VCC, Rain_drop_sensor.leg1, water_level_sensor.leg1, water_level_sensor.leg2, I2C_LCD.VCC, relay_fan.+, relay_pump.+, DHT11_1.VCC
  N12: Part1.D3_PWM, Ultrasonic_sensor.ECHO
  N13: Part1.D4_PWM, Ultrasonic_sensor.TRIG
  N14: Part1.D5_PWM, relay_pump.S
  N15: Part1.D53, relay_fan.S
  N16: relay_fan.Common, SERVO1.+5V, step_down(_motor_servo).OUT+
  N17: relay_fan.NO, motor_fan.pin_1
  N18: relay_pump.Common, step_down_(pump).OUT+
  N19: relay_pump.NO, Pump.pin_1
  N20: Red_led.anode, Resistor_redled.Pin_0
  N21: green_led.anode, resistor_green_led.Pin_0
  N22: BAT1.+, BAT2.-
  N23: BAT2.+, step_down(_motor_servo).IN+, step_down_(pump).IN+

custom parts:
  LCD1602-I2C: A standard character display, usually with 2x16 characters. Comes in many colors with LCM1602 IIC attached.
  KY-019 5V Relay Module: KY-019 5V Relay module, used to control AC circuits. (Special thanks to vanepp for fixing the PCB holes and other errors)
  Tower Pro SG90 servo: Original file by John De Cristofaro http://www.adafruit.com/products/1449 Adafruit Feedback Servo (Small) Edited by: e-radionica.com 28/9/2015
  Passive buzzer: Passive buzzer 12 mm, 3-5 V
  DHT11 module: https://cdn-learn.adafruit.com/downloads/pdf/dht.pdf DHT11 black pcb module reference by:https://github.com/adafruit/Fritzing-Library/blob/master/parts/DHT11%20Humitidy%20and%20Temperature%20Sensor.fzpz
  LM2596 step down module: LM2596 DC-DC step down power supply module 3 A.

// code stored in the sketch: projet.ino
// 1. Include the Libraries
#include <IRremote.hpp>
#include <IskakINO_LiquidCrystal_I2C.h>
#include <DHT.h>
#include <Servo.h>    // NEW: Include standard Servo library

// 2. Define all the Pins
int IR_PIN = 2;    
int ECHO_PIN = 3;  
int TRIG_PIN = 4;
int PUMP_RELAY = 5;   
int SERVO_PIN = 6;    // NEW: Servo Motor Signal Pin
int WATER_PIN = A8; 
int LIGHT_PIN = A12;  
int RAIN_PIN = A10;   
int SOIL_PIN = A1;    
int GREEN_LED = 10;
int RED_LED = 11;
int BUZZER = 12;      
int DHT_PIN = 13;
int FAN_RELAY = 52;   

// 3. Setup Objects
LiquidCrystal_I2C lcd(16, 2); 
DHT dht(DHT_PIN, DHT11);
Servo roofServo;      // NEW: Create Servo object to control the roof

// 4. Variables for our Passcode System
String correctPassword = "#123";
String enteredPassword = "";

// 5. System Modes
int systemMode = 0; 

// 6. Threshold Settings & Calibration Baselines
int intruderDistance = 5; 
int consecutiveTriggers = 0; 
int SOIL_THRESHOLD = 35; 
int STORM_THRESHOLD = 70; // NEW: Rain threshold percentage for a heavy storm

// 7. Non-Blocking Timers
unsigned long timerStart = 0;
unsigned long screenTimer = 0;
unsigned long blinkTimer = 0;
unsigned long fanTimer = 0; 
unsigned long pumpTimer = 0;    
unsigned long roofTimer = 0;    // NEW: Non-blocking timer for the roof servo
unsigned long serialTimer = 0; 
unsigned long alarmScreenTimer = 0; 

// Timers to manually oscillate the AC buzzer without crashing the IR Remote timer
unsigned long buzzerMicros = 0;
bool buzzerPinState = false;
bool shouldSound = false; 

// Screen Rotation State: 0 = Climate, 1 = Water Level, 2 = Light & Rain, 3 = Soil Moisture
int screenPage = 0; 
bool alarmToggleState = false; 

void setup() {
  Serial.begin(9600);
  
  pinMode(TRIG_PIN, OUTPUT);
  pinMode(ECHO_PIN, INPUT);
  pinMode(GREEN_LED, OUTPUT);
  pinMode(RED_LED, OUTPUT);
  pinMode(BUZZER, OUTPUT);
  pinMode(WATER_PIN, INPUT); 
  pinMode(LIGHT_PIN, INPUT); 
  pinMode(RAIN_PIN, INPUT);
  pinMode(SOIL_PIN, INPUT); 
  pinMode(FAN_RELAY, OUTPUT); 
  pinMode(PUMP_RELAY, OUTPUT); 
  
  // Initialize Servo
  roofServo.attach(SERVO_PIN); // NEW: Attach the servo to Pin 6
  roofServo.write(0);          // NEW: Ensure roof starts CLOSED (0 degrees) on boot
  
  // Ensure relays are turned OFF on boot (Assuming standard Active-LOW relay board)
  digitalWrite(FAN_RELAY, HIGH);
  digitalWrite(PUMP_RELAY, HIGH);
  
  IrReceiver.begin(IR_PIN);
  dht.begin();
  
  lcd.begin();         
  lcd.backlight();
  
  // BOOT WARM-UP & CALIBRATION PERIOD
  lcd.clear();
  lcd.setCursor(0, 0);
  lcd.print("System Booting...");
  
  for (int i = 3; i > 0; i--) {
    lcd.setCursor(0, 1);
    lcd.print("Arming in: "); lcd.print(i); lcd.print("s ");
    getDistance(); 
    delay(1000);
  }
  
  lockGreenhouse();
}

void loop() {
  checkRemote();
  unsigned long currentTime = millis();

  // ------------------------------------------------------------------
  // Global Serial Monitor Telemetry (Runs every 2 seconds)
  // ------------------------------------------------------------------
  if (currentTime - serialTimer >= 2000) {
    serialTimer = currentTime;
    
    float currentTemp = getTemperature();
    float currentHum = getHumidity();
    int waterLevel = getWaterLevel();
    int lightPercentage = getLightLevel();
    int rainPercentage = getRainLevel();
    int soilPercentage = getSoilMoisture(); 
    
    Serial.println("--- GREENHOUSE SYSTEM STATUS ---");
    Serial.print("Active Mode: "); Serial.println(systemMode);
    
    if (!isnan(currentTemp) && !isnan(currentHum)) {
      Serial.print("Temperature: "); Serial.print(currentTemp, 1); Serial.println(" C");
      Serial.print("Humidity   : "); Serial.print(currentHum, 1); Serial.println(" %");
    } else {
      Serial.println("Temperature/Humidity: Error reading DHT sensor!");
    }
    
    Serial.print("Water Level: "); Serial.print(waterLevel);
    if (waterLevel == 0)      Serial.println(" (DRY)");
    else if (waterLevel == 1) Serial.println(" (LOW)");
    else if (waterLevel == 2) Serial.println(" (MED)");
    else if (waterLevel == 3) Serial.println(" (HIGH)");
    
    Serial.print("Light Level: "); Serial.print(lightPercentage); Serial.println(" %");
    Serial.print("Rain Fall  : "); Serial.print(rainPercentage); Serial.println(" %");
    Serial.print("Soil Moist : "); Serial.print(soilPercentage); Serial.println(" %"); 
    Serial.println("--------------------------------\n");
  }

  // ------------------------------------------------------------------
  // Automatic Fan Temperature Control (Checks every 2 seconds)
  // ------------------------------------------------------------------
  if (currentTime - fanTimer >= 2000) {
    fanTimer = currentTime;
    float currentTemp = getTemperature();
    
    if (!isnan(currentTemp)) {
      if (currentTemp > 30) {
        digitalWrite(FAN_RELAY, LOW);   // Turn fan ON
      } else {
        digitalWrite(FAN_RELAY, HIGH);  // Turn fan OFF
      }
    }
  }

  // ------------------------------------------------------------------
  // Automatic Irrigation Pump Control (Checks every 2 seconds)
  // ------------------------------------------------------------------
  if (currentTime - pumpTimer >= 2000) {
    pumpTimer = currentTime;
    int currentSoilMoisture = getSoilMoisture();
    
    if (currentSoilMoisture <= SOIL_THRESHOLD) {
      digitalWrite(PUMP_RELAY, LOW);   // Turn pump ON
    } else {
      digitalWrite(PUMP_RELAY, HIGH);  // Turn pump OFF
    }
  }

  // ------------------------------------------------------------------
  // NEW: Automatic Roof Servo Control (Checks every 2 seconds)
  // ------------------------------------------------------------------
  if (currentTime - roofTimer >= 2000) {
    roofTimer = currentTime;
    int lightPercentage = getLightLevel();
    int rainPercentage = getRainLevel();
    
    // Open if light is bright (>50%) AND there is no heavy storm (<70% rain)
    if (lightPercentage > 50 && rainPercentage < STORM_THRESHOLD) {
      roofServo.write(90);  // 90 Degrees = Open State
    } else {
      roofServo.write(0);   // 0 Degrees = Closed State (Night or Storm)
    }
  }

  // Security System Logic
  if (systemMode == 0) {
    float distance = getDistance();
    if (distance > 0.5 && distance < intruderDistance) { 
      consecutiveTriggers++;
      if (consecutiveTriggers >= 3) {
        triggerAlarm();
      }
    } else {
      consecutiveTriggers = 0; 
    }
  } 
  else if (systemMode == 1) { 
    digitalWrite(GREEN_LED, HIGH);
    updateScreen(currentTime);

    if (currentTime - timerStart >= 10000) {
      systemMode = 2; 
      digitalWrite(GREEN_LED, LOW); 
    }
  } 
  else if (systemMode == 2) { 
    updateScreen(currentTime); 

    float distance = getDistance();
    if (distance > 0.5 && distance < intruderDistance) { 
      consecutiveTriggers++;
      if (consecutiveTriggers >= 3) {
        triggerAlarm();
      }
    } else {
      consecutiveTriggers = 0;
    }
  } 
  else if (systemMode == 3) { 
    if (currentTime - blinkTimer >= 250) {
      blinkTimer = currentTime; 
      alarmToggleState = !alarmToggleState; 
      
      digitalWrite(RED_LED, alarmToggleState);
      shouldSound = alarmToggleState; 
    }

    if (currentTime - alarmScreenTimer >= 300) {
      alarmScreenTimer = currentTime;
      float distance = getDistance();
      
      lcd.setCursor(0, 0);
      lcd.print("Dist: ");
      if(distance == 999) {
        lcd.print("Out of Range   ");
      } else {
        lcd.print(distance, 1);
        lcd.print(" cm    "); 
      }
    }

    if (shouldSound == true) {
      unsigned long currentMicros = micros();
      if (currentMicros - buzzerMicros >= 500) { 
        buzzerMicros = currentMicros;
        buzzerPinState = !buzzerPinState;
        digitalWrite(BUZZER, buzzerPinState);
      }
    } else {
      digitalWrite(BUZZER, LOW); 
    }
  }
}

// ==========================================
//          CORE SYSTEM FUNCTIONS
// ==========================================

void checkRemote() {
  if (IrReceiver.decode()) {
    unsigned long code = IrReceiver.decodedIRData.decodedRawData;

    if (systemMode == 0 || systemMode == 3) {
      switch (code) {
        case 0xE916FF00: addNumber('1'); break;
        case 0xE619FF00: addNumber('2'); break;
        case 0xF20DFF00: addNumber('3'); break;
        case 0xF30CFF00: addNumber('4'); break;
        case 0xE718FF00: addNumber('5'); break;
        case 0xA15EFF00: addNumber('6'); break;
        case 0xF708FF00: addNumber('7'); break;
        case 0xE31CFF00: addNumber('8'); break;
        case 0xA55AFF00: addNumber('9'); break;
        case 0xAD52FF00: addNumber('0'); break;
        case 0xB54AFF00: addNumber('#'); break;
        
        case 0xBD42FF00: 
          enteredPassword = "";
          lcd.setCursor(6, 1);
          lcd.print("          "); 
          break;
          
        case 0xBF40FF00: 
          verifyPassword();
          break;
      }
    }
    IrReceiver.resume(); 
  }
}

void addNumber(char num) {
  enteredPassword += num;
  lcd.setCursor(6, 1); 
  lcd.print(enteredPassword);
}

void verifyPassword() {
  if (enteredPassword == correctPassword) {
    enteredPassword = "";
    shouldSound = false; 
    consecutiveTriggers = 0;
    
    digitalWrite(RED_LED, LOW);
    digitalWrite(BUZZER, LOW); 
    
    lcd.clear();
    lcd.setCursor(0, 0); 
    lcd.print("Code Matched!");
    lcd.setCursor(0, 1); 
    lcd.print("Opening Gate...");
    delay(1500); 
    lcd.clear();
    
    timerStart = millis(); 
    systemMode = 1; 
  } else {
    lcd.clear();
    lcd.setCursor(0,0);
    lcd.print("Access Denied!");
    delay(1000);
    
    enteredPassword = "";
    lcd.clear();
    if (systemMode == 3) {
      lcd.setCursor(0, 1);
      lcd.print("Code: ");
    } else {
      lockGreenhouse();
    }
  }
}

void lockGreenhouse() {
  systemMode = 0;
  enteredPassword = "";
  shouldSound = false;
  consecutiveTriggers = 0;
  digitalWrite(GREEN_LED, LOW);
  digitalWrite(RED_LED, LOW);
  digitalWrite(BUZZER, LOW);
  digitalWrite(FAN_RELAY, HIGH); 
  digitalWrite(PUMP_RELAY, HIGH); 
  roofServo.write(0);             // NEW: Securely close the roof when system is locked down
  lcd.clear();
  lcd.setCursor(0, 0); 
  lcd.print("Gate Code:"); 
}

void triggerAlarm() {
  systemMode = 3; 
  enteredPassword = ""; 
  lcd.clear();
  lcd.setCursor(0, 1);
  lcd.print("Code: "); 
}

void updateScreen(unsigned long currentTime) {
  if (currentTime - screenTimer >= 5000) {
    screenTimer = currentTime;
    screenPage++;
    if(screenPage > 3) screenPage = 0; 
    lcd.clear();
  }

  if (screenPage == 0) {
    float temp = getTemperature();
    float hum = getHumidity();
    
    lcd.setCursor(0, 0);
    lcd.print("Temp: ");
    lcd.print(temp, 1);
    lcd.print(" C   ");
    
    lcd.setCursor(0, 1);
    lcd.print("Hum:  ");
    lcd.print(hum, 1);
    lcd.print(" %   ");
  } 
  else if (screenPage == 1) {
    int waterLevel = getWaterLevel();
    
    lcd.setCursor(0, 0);
    lcd.print("Water Reservoir");
    lcd.setCursor(0, 1);
    lcd.print("Level: ");
    
    if (waterLevel == 0)      lcd.print("DRY   ");
    else if (waterLevel == 1) lcd.print("LOW   ");
    else if (waterLevel == 2) lcd.print("MED   ");
    else if (waterLevel == 3) lcd.print("HIGH  ");
  } 
  else if (screenPage == 2) {
    int lightPercentage = getLightLevel();
    int rainPercentage = getRainLevel();
    
    lcd.setCursor(0, 0);
    lcd.print("Light: ");
    lcd.print(lightPercentage);
    lcd.print("%    ");
    
    lcd.setCursor(0, 1);
    lcd.print("Rain:  ");
    lcd.print(rainPercentage);
    lcd.print("%    ");
  }
  else if (screenPage == 3) {
    int soilPercentage = getSoilMoisture();
    
    lcd.setCursor(0, 0);
    lcd.print("Soil Moisture");
    lcd.setCursor(0, 1);
    lcd.print("Level: ");
    lcd.print(soilPercentage);
    lcd.print("%    ");
  }
}

// ==========================================
//          HARDWARE SENSOR FUNCTIONS
// ==========================================

float getTemperature() { return dht.readTemperature(); }
float getHumidity() { return dht.readHumidity(); }

int getWaterLevel() {
  int rawValue = analogRead(WATER_PIN); 
  if (rawValue < 50)   return 0; 
  if (rawValue < 300)  return 1; 
  if (rawValue < 600)  return 2; 
  return 3; 
}

int getLightLevel() {
  int rawLight = analogRead(LIGHT_PIN);
  return map(rawLight, 0, 1023, 0, 100);
}

int getRainLevel() {
  int rawRain = analogRead(RAIN_PIN);
  int percentage = map(rawRain, 1023, 0, 0, 100);
  if(percentage < 0) percentage = 0;
  return percentage;
}

int getSoilMoisture() {
  int rawSoil = analogRead(SOIL_PIN);
  int percentage = map(rawSoil, 1023, 250, 0, 100);
  return constrain(percentage, 0, 100); 
}

float getDistance() {
  digitalWrite(TRIG_PIN, LOW);
  delayMicroseconds(2);
  digitalWrite(TRIG_PIN, HIGH);
  delayMicroseconds(10);
  digitalWrite(TRIG_PIN, LOW);
  
  long duration = pulseIn(ECHO_PIN, HIGH, 30000); 
  if (duration == 0) return 999; 
  
  return duration * 0.034 / 2; 
}
